// Logisim project LC-3-v2.circ as structural Verilog: 17 circuits, main circuit main
// RES
module main (
  input  Reset,
  output out_2,
  output out_3,
  output out_4,
  output out_5,
  output out_6,
  output out_7,
  output out_8,
  output [15:0] out_9,
  output [15:0] out_10,
  output [15:0] out_11,
  output [15:0] out_12,
  output [15:0] out_13,
  output [15:0] out_14,
  output [15:0] out_15,
  output [15:0] out_16,
  output [15:0] out_17,
  output halt,
  output [15:0] out_19,
  output [15:0] out_20,
  output [15:0] out_21,
  output [15:0] out_22
);

  wire decodeir_1_p5, getcst_1_usecst, or16_1_out_2, or16_2_out_2, ramctrl_1_memload, ramctrl_1_memstore;
  wire [2:0] nzp_1_out_4;
  wire [15:0] alu_1_output, getcst_1_cst, RegIN, registres_1_out_sr1, registres_1_out_sr2;

  BiClock biclock_1 (.reset(Reset), .signal0(out_2), .signal1(out_3));
  RegPC regpc_1 (
    .H(out_3), .PC(out_9), .Reset(Reset), .IR(out_10), .R(registres_1_out_sr1), .TestNZP(out_5), .Jump(out_4));
  // Probe on out_9
  // Probe on out_11
  GetAddr getaddr_1 (.PC(out_9), .BaseR(registres_1_out_sr1), .IR(out_10), .Addr(out_11), .Fetch(out_2));
  // Probe on out_12
  LED led_1 (.in(out_6));
  RamCtrl ramctrl_1 (
    .Store(out_7), .Fetch(out_2), .Exec(out_3), .Load(out_6), .MemStore(ramctrl_1_memstore),
    .MemLoad(ramctrl_1_memload));
  LED led_2 (.in(out_7));
  // Probe on out_13
  RAM #(.addrWidth(16), .dataWidth(16), .bus("separate")) ram_1 (
    .addr(out_11), .din(out_12), .data(out_13), .str(ramctrl_1_memstore), .clk(ramctrl_1_memstore),
    .ld(ramctrl_1_memload));  // open: sel, clr
  Register #(.width(16), .trigger("falling")) RegIR (.D(out_13), .Q(out_10), .clk(out_2));  // open: en, clr
  // DecodeIR decodeir_1: pin names not known; wires that end beside it: out_6, out_7, out_4, out_10, decodeir_1_p5
  // Probe on out_10[11:9]
  // Probe on out_10[8:6]
  // Probe on out_10[2:0]
  // Probe on getcst_1_cst
  GetCst getcst_1 (.IR(out_10), .Cst(getcst_1_cst), .UseCst(getcst_1_usecst));
  // Probe on out_10[15:14]
  and and_1 (out_8, decodeir_1_p5, out_3);
  Registres registres_1 (
    .SR1(out_10[8:6]), .IN(RegIN), .SR2(out_10[2:0]), .WriteReg(out_8), .DR_SR(out_10[11:9]),
    .OUT_SR1(registres_1_out_sr1), .OUT_SR2(registres_1_out_sr2), .OUT_SR(out_12), .R0(out_14), .R1(out_15),
    .R2(out_16), .R3(out_17), .R4(out_19), .R5(out_20), .R6(out_21), .R7(out_22));
  // Probe on registres_1_out_sr1
  ALU alu_1 (
    .UseCst(getcst_1_usecst), .e2(out_10[15:14]), .Input1(registres_1_out_sr1), .Input2(registres_1_out_sr2),
    .Cst(getcst_1_cst), .Output(alu_1_output));
  // Probe on registres_1_out_sr2
  // Probe on alu_1_output
  NZP nzp_1 (.out_4(nzp_1_out_4), .WriteReg(out_8), .RES(RegIN), .TestNZP(out_5), .IR(out_10));
  // Probe on nzp_1_out_4
  Or16 or16_1 (.in_1(out_10), .out_2(or16_1_out_2));
  Or16 or16_2 (.in_1(out_9), .out_2(or16_2_out_2));
  // Probe on out_14
  // Probe on out_15
  // Probe on out_16
  // Probe on out_17
  // Probe on out_19
  // Probe on out_20
  // Probe on out_21
  // Probe on out_22
  and and_2 (halt, ~or16_1_out_2, or16_2_out_2);  // AND_Gate
  WriteVal writeval_1 (.Load(out_6), .ALURes(alu_1_output), .MemOUT(out_13), .IR(out_10), .PC(out_9), .RegIN(RegIN));

  // Other names for the same wires on the sheet: Addr[15:0] = out_11; Condition = out_5; Exec = out_3; Fetch = out_2;
  //   IR[15:0] = out_10; JumpInstr = out_4; Load = out_6; MemIN[15:0] = out_12; MemOUT[15:0] = out_13;
  //   PC[15:0] = out_9; R0[15:0] = out_14; R1[15:0] = out_15; R2[15:0] = out_16; R3[15:0] = out_17; R4[15:0] = out_19;
  //   R5[15:0] = out_20; R6[15:0] = out_21; R7[15:0] = out_22; Store = out_7; WriteReg = out_8

  // Notes on the sheet:
  //   R
  //   IR
  //   R
  //   IR
  //   RAM
  //   Traces (NE PAS MODIFIER)______________________________________________________________________________________________________
  //   GetOp
  //   Arret des traces au 1er NOP
endmodule

module ALU (
  input  [15:0] Input1,
  input  [15:0] Input2,
  input  [15:0] Cst,
  input  UseCst,
  input  [1:0] e2,
  output [15:0] Output
);

  wire [15:0] adder_1_out, and_1_out, bsb_bsf_1_out_4, multiplexer_1_out, not_1_out;

  Multiplexer #(.width(16), .enable("false")) multiplexer_1 (
    .in0(Input2), .in1(Cst), .out(multiplexer_1_out), .sel(UseCst));
  Adder #(.width(16)) adder_1 (.a(multiplexer_1_out), .b(Input1), .out(adder_1_out));  // open: cin, cout
  assign and_1_out = Input1 & multiplexer_1_out;  // AND_Gate and_1, 16 bits wide
  Multiplexer #(.select(2), .width(16), .enable("false")) multiplexer_2 (
    .in0(adder_1_out), .in1(and_1_out), .in2(not_1_out), .in3(bsb_bsf_1_out_4), .out(Output), .sel(e2));
  BSB_BSF bsb_bsf_1 (.Input(Input1), .IR__bit5(UseCst), .cste(multiplexer_1_out), .out_4(bsb_bsf_1_out_4));
  assign not_1_out = ~Input1;  // NOT_Gate not_1, 16 bits wide

  // Notes on the sheet:
  //   e2 doit être 11 pour BSB/BSF
  //   A COMPLETER v1
endmodule

module reverse16 (
  input  [15:0] Input2,
  output [15:0] out_2
);


  assign out_2 = {Input2[0], Input2[1], Input2[2], Input2[3], Input2[4], Input2[5], Input2[6], Input2[7], Input2[8], Input2[9], Input2[10], Input2[11], Input2[12], Input2[13], Input2[14], Input2[15]};
endmodule

module BSB_BSF (
  input  [15:0] Input,
  input  IR__bit5,
  input  [15:0] cste,
  output [15:0] out_4
);

  wire [3:0] priority_encoder_1_out;
  wire [15:0] bit_extender_1_out, multiplexer_1_out, reverse16_1_out_2, subtractor_1_out;

  reverse16 reverse16_1 (.Input2(Input), .out_2(reverse16_1_out_2));
  Multiplexer #(.width(16), .enable("false")) multiplexer_1 (
    .in0(Input), .in1(reverse16_1_out_2), .out(multiplexer_1_out), .sel(IR__bit5));
  Priority_Encoder #(.select(4)) priority_encoder_1 (
    .in0(multiplexer_1_out[0]), .in1(multiplexer_1_out[1]), .in2(multiplexer_1_out[2]),
    .in3(multiplexer_1_out[3]), .in4(multiplexer_1_out[4]), .in5(multiplexer_1_out[5]),
    .in6(multiplexer_1_out[6]), .in7(multiplexer_1_out[7]), .in8(multiplexer_1_out[8]),
    .in9(multiplexer_1_out[9]), .in10(multiplexer_1_out[10]), .in11(multiplexer_1_out[11]),
    .in12(multiplexer_1_out[12]), .in13(multiplexer_1_out[13]), .in14(multiplexer_1_out[14]),
    .in15(multiplexer_1_out[15]), .out(priority_encoder_1_out));  // open: gs, en_out, en_in
  assign bit_extender_1_out = {{12{1'b0}}, priority_encoder_1_out};  // Bit_Extender bit_extender_1
  Subtractor #(.width(16)) subtractor_1 (.a(cste), .b(bit_extender_1_out), .out(subtractor_1_out));  // open: bin, bout
  Multiplexer #(.width(16), .enable("false")) multiplexer_2 (
    .in0(bit_extender_1_out), .in1(subtractor_1_out), .out(out_4), .sel(IR__bit5));
endmodule

module DecodeIR (
  input  [15:0] IR,
  output Jump,
  output Arith,
  output WriteReg,
  output Load,
  output Store
);

  wire and_1_out, multiplexer_1_out;

  Demultiplexer #(.select(2), .enable("false")) demultiplexer_1 (
    .out0(Jump), .out1(Arith), .out2(Load), .out3(Store), .in(1'b1), .sel(IR[13:12]));
  Multiplexer #(.select(2), .enable("false")) multiplexer_1 (
    .in0(1'b0), .in1(1'b1), .in2(1'b0), .in3(1'b0), .out(multiplexer_1_out), .sel(IR[15:14]));
  and and_1 (and_1_out, multiplexer_1_out, Jump);
  or or_1 (WriteReg, and_1_out, Arith, Load);
endmodule

module GetAddr (
  input  [15:0] IR,
  input  Fetch,
  input  [15:0] PC,
  input  [15:0] BaseR,
  output [15:0] Addr
);

  wire or_1_out;
  wire [15:0] adder_1_out, adder_2_out, multiplexer_1_out, offset6_1_off6, offset9_1_off9;

  Offset9 offset9_1 (.IR(IR), .Off9(offset9_1_off9));
  Offset6 offset6_1 (.IR(IR), .Off6(offset6_1_off6));
  Adder #(.width(16)) adder_1 (.a(offset6_1_off6), .b(BaseR), .out(adder_1_out));  // open: cin, cout
  Adder #(.width(16)) adder_2 (.a(offset9_1_off9), .b(PC), .out(adder_2_out), .cin(1'b1));  // open: cout
  Multiplexer #(.width(16), .disabled(0), .enable("false")) multiplexer_1 (
    .in0(adder_2_out), .in1(adder_1_out), .out(multiplexer_1_out), .sel(IR[14]));
  or or_1 (or_1_out, ~IR[13], Fetch);  // OR_Gate
  Multiplexer #(.width(16), .disabled(0), .enable("false")) multiplexer_2 (
    .in0(multiplexer_1_out), .in1(PC), .out(Addr), .sel(or_1_out));

  // Notes on the sheet:
  //   PC+SEXT(Offset6)
  //   b14: label or BaseR?
  //   PC+SEXT(Offset9)
  //   b13: Load ou Store?
  //   Pourquoi ?
endmodule

module GetCst (
  input  [15:0] IR,
  output [15:0] Cst,
  output UseCst
);

  assign Cst = {{11{IR[4]}}, IR[4:0]};  // Bit_Extender bit_extender_1

  assign UseCst = IR[5];
endmodule

module Offset11 (
  output [15:0] SEXTOff11,
  output [15:0] IR
);

  assign SEXTOff11 = {{5{1'b0}}, IR[10:0]};  // Bit_Extender bit_extender_1
endmodule

module NZP (
  input  [15:0] RES,
  input  WriteReg,
  input  [15:0] IR,
  output [2:0] out_4,
  output TestNZP
);

  wire [2:0] and_1_out, comparator_1_lt;

  Comparator #(.width(16)) comparator_1 (
    .a({16{1'b0}}), .b(RES), .gt(comparator_1_lt[2]), .eq(comparator_1_lt[1]), .lt(comparator_1_lt[0]));
  Multiplexer #(.width(3), .enable("false")) multiplexer_1 (
    .in0(out_4), .in1(comparator_1_lt), .out(out_4), .sel(WriteReg));
  // Probe on IR[11:9]
  assign and_1_out = out_4 & IR[11:9];  // AND_Gate and_1, 3 bits wide
  or or_1 (TestNZP, and_1_out[0], and_1_out[1], and_1_out[2]);

  // Notes on the sheet:
  //   (Resultat du calcul courant)
  //   (Instruction courante)
endmodule

module BiClock (
  input  reset,
  output signal0,
  output signal1
);

  wire and_1_out, horloge_out, not_1_out, register_1_q;

  Clock horloge (.out(horloge_out));
  not not_1 (not_1_out, register_1_q);
  Register #(.width(1), .trigger("falling")) register_1 (
    .D(not_1_out), .Q(register_1_q), .clk(horloge_out), .clr(reset));  // open: en
  and and_1 (and_1_out, horloge_out, ~reset);  // AND_Gate
  and and_2 (signal0, ~register_1_q, and_1_out);  // AND_Gate
  and and_3 (signal1, register_1_q, and_1_out);

  // Notes on the sheet:
  //   Ce module divise une horloge en deux sous-horloges alternées
  //   Chronogrammes :
  //   horloge: 0101010101 signal0: 0100010001 signal1: 000100010
  //   registre 1-bit
  //   Enable
  //   select : 0 / 1
endmodule

// Off6
module Offset6 (
  input  [15:0] IR,
  output [15:0] Off6
);

  assign Off6 = {{10{IR[5]}}, IR[5:0]};  // Bit_Extender bit_extender_1
endmodule

// Off9
module Offset9 (
  input  [15:0] IR,
  output [15:0] Off9
);

  assign Off9 = {{7{IR[8]}}, IR[8:0]};  // Bit_Extender bit_extender_1
endmodule

module Or16 (
  input  [15:0] in_1,
  output out_2
);

  wire [1:0] or_2_out;
  wire [7:0] or_1_out;

  assign or_1_out = in_1[7:0] | in_1[15:8];  // OR_Gate or_1, 8 bits wide
  assign or_2_out = or_1_out[1:0] | or_1_out[3:2] | or_1_out[5:4] | or_1_out[7:6];  // OR_Gate or_2, 2 bits wide
  or or_3 (out_2, or_2_out[0], or_2_out[1]);
endmodule

module RamCtrl (
  input  Exec,
  input  Fetch,
  input  Load,
  input  Store,
  output MemLoad,
  output MemStore
);

  wire and_1_out;

  and and_1 (and_1_out, Exec, Load);
  and and_2 (MemStore, Exec, Store);
  or or_1 (MemLoad, Fetch, and_1_out);
endmodule

module Registres (
  input  [2:0] SR1,
  input  [15:0] IN,
  input  [2:0] SR2,
  input  WriteReg,
  input  [2:0] DR_SR,
  output [15:0] R0,
  output [15:0] OUT_SR1,
  output [15:0] R1,
  output [15:0] R2,
  output [15:0] R3,
  output [15:0] OUT_SR2,
  output [15:0] R4,
  output [15:0] R5,
  output [15:0] OUT_SR,
  output [15:0] R6,
  output [15:0] R7
);

  wire decoder_1_out0, decoder_1_out1, decoder_1_out2, decoder_1_out3, decoder_1_out4, decoder_1_out5,
       decoder_1_out6, decoder_1_out7;

  Decoder #(.select(3), .disabled(0)) decoder_1 (
    .out0(decoder_1_out0), .out1(decoder_1_out1), .out2(decoder_1_out2), .out3(decoder_1_out3),
    .out4(decoder_1_out4), .out5(decoder_1_out5), .out6(decoder_1_out6), .out7(decoder_1_out7), .sel(DR_SR),
    .en(WriteReg));
  Register #(.width(16), .trigger("falling")) u_R0 (.D(IN), .Q(R0), .clk(decoder_1_out0));  // open: en, clr
  Register #(.width(16), .trigger("falling")) u_R1 (.D(IN), .Q(R1), .clk(decoder_1_out1));  // open: en, clr
  Register #(.width(16), .trigger("falling")) u_R2 (.D(IN), .Q(R2), .clk(decoder_1_out2));  // open: en, clr
  Register #(.width(16), .trigger("falling")) u_R3 (.D(IN), .Q(R3), .clk(decoder_1_out3));  // open: en, clr
  Register #(.width(16), .trigger("falling")) u_R4 (.D(IN), .Q(R4), .clk(decoder_1_out4));  // open: en, clr
  Register #(.width(16), .trigger("falling")) u_R5 (.D(IN), .Q(R5), .clk(decoder_1_out5));  // open: en, clr
  Register #(.width(16), .trigger("falling")) u_R6 (.D(IN), .Q(R6), .clk(decoder_1_out6));  // open: en, clr
  Register #(.width(16), .trigger("falling")) u_R7 (.D(IN), .Q(R7), .clk(decoder_1_out7));  // open: en, clr
  Multiplexer #(.select(3), .width(16), .enable("false")) multiplexer_1 (
    .in0(R0), .in1(R1), .in2(R2), .in3(R3), .in4(R4), .in5(R5), .in6(R6), .in7(R7), .out(OUT_SR1), .sel(SR1));
  Multiplexer #(.select(3), .width(16), .enable("false")) multiplexer_2 (
    .in0(R0), .in1(R1), .in2(R2), .in3(R3), .in4(R4), .in5(R5), .in6(R6), .in7(R7), .out(OUT_SR2), .sel(SR2));
  Multiplexer #(.select(3), .width(16), .enable("false")) multiplexer_3 (
    .in0(R0), .in1(R1), .in2(R2), .in3(R3), .in4(R4), .in5(R5), .in6(R6), .in7(R7), .out(OUT_SR), .sel(DR_SR));
endmodule

module RegPC (
  input  [15:0] IR,
  input  H,
  input  [15:0] R,
  input  Reset,
  input  Jump,
  input  TestNZP,
  output [15:0] PC
);

  wire and_1_out, and_2_out, or_1_out;
  wire [15:0] adder_1_out, adder_2_out, multiplexer_1_out, multiplexer_2_out, multiplexer_3_out,
       offset9_1_off9;

  and and_1 (and_1_out, IR[14], Jump);
  and and_2 (and_2_out, Jump, TestNZP);
  Offset9 offset9_1 (.IR(IR), .Off9(offset9_1_off9));
  or or_1 (or_1_out, and_1_out, and_2_out);
  Adder #(.width(16)) adder_1 (.a(PC), .b(16'h1), .out(adder_1_out));  // open: cin, cout
  Multiplexer #(.width(16), .disabled(0), .enable("false")) multiplexer_1 (
    .in0(offset9_1_off9), .in1({16{1'b0}}), .out(multiplexer_1_out), .sel(and_1_out));
  Adder #(.width(16)) adder_2 (.a(adder_1_out), .b(multiplexer_1_out), .out(adder_2_out));  // open: cin, cout
  Multiplexer #(.width(16), .disabled(0), .enable("false")) multiplexer_2 (
    .in0(adder_2_out), .in1(R), .out(multiplexer_2_out), .sel(and_1_out));
  Multiplexer #(.width(16), .enable("false")) multiplexer_3 (
    .in0(adder_1_out), .in1(multiplexer_2_out), .out(multiplexer_3_out), .sel(or_1_out));
  Register #(.width(16), .trigger("falling")) u_PC (.D(multiplexer_3_out), .Q(PC), .clk(H), .clr(Reset));  // open: en

  // Notes on the sheet:
  //   A COMPLETER v2
  //   pour BR
  //   pour JSR
  //   JSR ssi JMP et 14
  //   PC <- PC + 1
  //   A COMPLETER v2
  //   PC+Off
  //   BaseR
  //   BaseR ssi JMP ou JSRR
  //   saut ssi JMP et (BR =>TestNZP)
  //   pas saut
  //   saut
endmodule

module WriteVal (
  input  [15:0] ALURes,
  input  [15:0] MemOUT,
  input  [15:0] PC,
  input  [15:0] IR,
  input  Load,
  output [15:0] RegIN
);

  wire JSR, LEA;
  wire [1:1] or_1_out;
  wire [15:0] adder_1_out, offset9_1_off9;

  and and_1 (LEA, ~IR[12], IR[13], IR[14], IR[15]);  // AND_Gate
  and and_2 (JSR, ~IR[12], ~IR[13], IR[14], ~IR[15]);  // AND_Gate
  Offset9 offset9_1 (.IR(IR), .Off9(offset9_1_off9));
  Adder #(.width(16)) adder_1 (.a(offset9_1_off9), .b(PC), .out(adder_1_out));  // open: cin, cout
  or or_1 (or_1_out[1], LEA, JSR);
  Multiplexer #(.select(2), .width(16)) multiplexer_1 (
    .in0(ALURes), .in1(MemOUT), .in2(adder_1_out), .in3(PC), .out(RegIN), .sel({or_1_out[1], Load}), .en(Load));

  // Notes on the sheet:
  //   A COMPLETER v1 et v2 :
  //   RegIN = si JSR alors PC sinon si LEA alors PC+SEXT(Offset9) sinon si Load alors MemOUT sinon ALURes  
endmodule
